// Logisim project guess-the-number.circ as structural Verilog: 4 circuits, main circuit main
module main (
  input  Pause,
  input  Config
);

  wire Clear_out, clock_1_out, \cronômetro_1_end , DM_out, DS_out, UM_out, US_out;
  wire [3:0] \cronômetro_1_dezena_de_minuto , \cronômetro_1_dezena_de_segundo ,
       \cronômetro_1_unidade_de_minuto , \cronômetro_1_unidade_de_segundo ;

  LED End (.in(\cronômetro_1_end ));
  Button DM (.out(DM_out));
  Hex_Digit_Display hex_digit_display_1 (.value(\cronômetro_1_unidade_de_minuto ));  // open: dp
  Hex_Digit_Display hex_digit_display_2 (.value(\cronômetro_1_dezena_de_minuto ));  // open: dp
  Button UM (.out(UM_out));
  Button DS (.out(DS_out));
  Hex_Digit_Display hex_digit_display_3 (.value(\cronômetro_1_dezena_de_segundo ));  // open: dp
  Button US (.out(US_out));
  Hex_Digit_Display hex_digit_display_4 (.value(\cronômetro_1_unidade_de_segundo ));  // open: dp
  \Cronômetro  \cronômetro_1  (
    .End(\cronômetro_1_end ), .Dezena_de_minuto(\cronômetro_1_dezena_de_minuto ),
    .Unidade_de_minuto(\cronômetro_1_unidade_de_minuto ),
    .Dezena_de_segundo(\cronômetro_1_dezena_de_segundo ),
    .Unidade_de_segundo(\cronômetro_1_unidade_de_segundo ), .Clock(clock_1_out), .Pause(Pause),
    .Config(Config), .Clear(Clear_out), .Altera_dezena_de_minuto(DM_out), .Altera_unidade_de_minuto(UM_out),
    .Altera_dezena_de_segundo(DS_out), .Altera_unidade_de_segundo(US_out));
  Button Clear (.out(Clear_out));
  Clock clock_1 (.out(clock_1_out));
endmodule

module Unidade (
  input  Clear,
  input  Clk,
  input  Alterar,
  input  Mode,
  input  Pause,
  output [3:0] Valor,
  output \Sinal_p__próximo 
);

  wire multiplexer_1_out, multiplexer_2_out, or_1_out, or_2_out;
  wire [3:0] subtractor_1_out;

  Subtractor #(.width(4)) subtractor_1 (.a(Valor), .b(4'b0001), .out(subtractor_1_out));  // open: bin, bout
  Multiplexer multiplexer_1 (.in0(Clk), .in1(Alterar), .out(multiplexer_1_out), .sel(Mode));  // open: en
  Multiplexer multiplexer_2 (.in0(multiplexer_1_out), .in1(1'b0), .out(multiplexer_2_out), .sel(Pause));  // open: en
  D_Flip_Flop d_ff_1 (
    .clk(multiplexer_2_out), .D(subtractor_1_out[3]), .Q(Valor[3]), .preset(\Sinal_p__próximo ), .reset(Clear));  // open: Qn, en
  D_Flip_Flop d_ff_2 (
    .clk(multiplexer_2_out), .D(subtractor_1_out[2]), .Q(Valor[2]), .reset(or_1_out));  // open: Qn, preset, en
  D_Flip_Flop d_ff_3 (
    .clk(multiplexer_2_out), .D(subtractor_1_out[1]), .Q(Valor[1]), .reset(or_2_out));  // open: Qn, preset, en
  D_Flip_Flop d_ff_4 (
    .clk(multiplexer_2_out), .D(subtractor_1_out[0]), .Q(Valor[0]), .preset(\Sinal_p__próximo ), .reset(Clear));  // open: Qn, en
  or or_1 (or_1_out, \Sinal_p__próximo , Clear);
  or or_2 (or_2_out, \Sinal_p__próximo , Clear);
  and and_1 (\Sinal_p__próximo , Valor[3], Valor[2], Valor[1], Valor[0]);
endmodule

module Dezena (
  input  Clear,
  input  Clk,
  input  Alterar,
  input  Mode,
  input  Pause,
  output [3:0] Valor,
  output \Sinal_p__próximo 
);

  wire multiplexer_1_out, multiplexer_2_out, or_1_out, or_2_out;
  wire [3:0] subtractor_1_out;

  Subtractor #(.width(4)) subtractor_1 (.a(Valor), .b(4'b0001), .out(subtractor_1_out));  // open: bin, bout
  Multiplexer multiplexer_1 (.in0(Clk), .in1(Alterar), .out(multiplexer_1_out), .sel(Mode));  // open: en
  Multiplexer multiplexer_2 (.in0(multiplexer_1_out), .in1(1'b0), .out(multiplexer_2_out), .sel(Pause));  // open: en
  D_Flip_Flop d_ff_1 (
    .clk(multiplexer_2_out), .D(subtractor_1_out[3]), .Q(Valor[3]), .reset(or_1_out));  // open: Qn, preset, en
  D_Flip_Flop d_ff_2 (
    .clk(multiplexer_2_out), .D(subtractor_1_out[2]), .Q(Valor[2]), .preset(\Sinal_p__próximo ), .reset(Clear));  // open: Qn, en
  D_Flip_Flop d_ff_3 (
    .clk(multiplexer_2_out), .D(subtractor_1_out[1]), .Q(Valor[1]), .reset(or_2_out));  // open: Qn, preset, en
  D_Flip_Flop d_ff_4 (
    .clk(multiplexer_2_out), .D(subtractor_1_out[0]), .Q(Valor[0]), .preset(\Sinal_p__próximo ), .reset(Clear));  // open: Qn, en
  or or_1 (or_1_out, Clear, \Sinal_p__próximo );
  or or_2 (or_2_out, Clear, \Sinal_p__próximo );
  and and_1 (\Sinal_p__próximo , Valor[3], Valor[2], Valor[1], Valor[0]);
endmodule

module \Cronômetro  (
  input  Clock,
  input  Clear,
  input  Altera_dezena_de_minuto,
  input  Altera_unidade_de_minuto,
  input  Altera_dezena_de_segundo,
  input  Altera_unidade_de_segundo,
  input  Pause,
  input  Config,
  output End,
  output [3:0] Dezena_de_minuto,
  output [3:0] Unidade_de_minuto,
  output [3:0] Dezena_de_segundo,
  output [3:0] Unidade_de_segundo
);

  wire and_2_out, and_3_out, and_4_out, and_5_out, \dezena_1_sinal_p__próximo , \dezena_2_sinal_p__próximo ,
       or_1_out, \unidade_1_sinal_p__próximo , \unidade_2_sinal_p__próximo ;

  and and_1 (End, and_2_out, and_3_out, and_4_out, and_5_out);
  and and_2 (and_2_out, ~Dezena_de_minuto[3], ~Dezena_de_minuto[2], ~Dezena_de_minuto[1], ~Dezena_de_minuto[0]);  // AND_Gate
  Dezena dezena_1 (
    .Clk(\unidade_1_sinal_p__próximo ), .Alterar(Altera_dezena_de_minuto),
    .\Sinal_p__próximo (\dezena_1_sinal_p__próximo ), .Clear(Clear), .Valor(Dezena_de_minuto),
    .Mode(or_1_out), .Pause(Pause));
  and and_3 (and_3_out, ~Unidade_de_minuto[3], ~Unidade_de_minuto[2], ~Unidade_de_minuto[1], ~Unidade_de_minuto[0]);  // AND_Gate
  Unidade unidade_1 (
    .\Sinal_p__próximo (\unidade_1_sinal_p__próximo ), .Mode(or_1_out), .Valor(Unidade_de_minuto),
    .Pause(Pause), .Clk(\dezena_2_sinal_p__próximo ), .Clear(Clear), .Alterar(Altera_unidade_de_minuto));
  and and_4 (and_4_out, ~Dezena_de_segundo[3], ~Dezena_de_segundo[2], ~Dezena_de_segundo[1], ~Dezena_de_segundo[0]);  // AND_Gate
  Dezena dezena_2 (
    .Clk(\unidade_2_sinal_p__próximo ), .Alterar(Altera_dezena_de_segundo),
    .\Sinal_p__próximo (\dezena_2_sinal_p__próximo ), .Clear(Clear), .Valor(Dezena_de_segundo),
    .Mode(or_1_out), .Pause(Pause));
  and and_5 (and_5_out, ~Unidade_de_segundo[3], ~Unidade_de_segundo[2], ~Unidade_de_segundo[1], ~Unidade_de_segundo[0]);  // AND_Gate
  Unidade unidade_2 (
    .\Sinal_p__próximo (\unidade_2_sinal_p__próximo ), .Mode(or_1_out), .Valor(Unidade_de_segundo),
    .Pause(Pause), .Clk(Clock), .Clear(Clear), .Alterar(Altera_unidade_de_segundo));
  or or_1 (or_1_out, End, Config);
endmodule
